# Fritzing sketch GPIO Switches (saved by Fritzing 0.9.3b)
breadboards: 1

parts:
  FET1 = STP16NF06 N-Channel Power MOSFET
  R1 = Resistor [tolerance=±5% resistance=4.7k package=THT]
  Raspberry_Pi1 = Raspberry Pi 2
  S1 = Momentary Switch [package=ksa_sealed_tac_switch]
  S2 = Momentary Switch [package=ksa_sealed_tac_switch]

nets:
  N1: FET1.gate, R1.Pin_0, Raspberry_Pi1.GPIO25
  N2: FET1.source, R1.Pin_1, S1.1, S2.1
  N3: Raspberry_Pi1.GND, S1.2
  N4: Raspberry_Pi1.GPIO24, S1.4
  N5: Raspberry_Pi1.GPIO23, S2.4

custom parts:
  STP16NF06 N-Channel Power MOSFET: STP16NF06 N-channel Power MOSFET
