# Fritzing sketch I2S Audio Board (saved by Fritzing 0.9.3b)
circuit board: 8.46667cm x 5.64444cm

parts:
  Raspberry_Pi_Zero1 = Raspberry Pi Zero
  Part1 = Adafruit MAX98357A I2S 3W Class D Amplifier [part_number="Adafruit #3006"]
  SP1 = SPEAKER [package=pcb_mount_speaker]

nets (from the breadboard view):
  N1: Raspberry_Pi_Zero1.GPIO19, Part1.LRCLK
  GND: Raspberry_Pi_Zero1.GND, Part1.GND
  N2: Raspberry_Pi_Zero1.GPIO21, Part1.DIN
  N3: Raspberry_Pi_Zero1.GPIO18, Part1.BCLK
  5V: Raspberry_Pi_Zero1.5V, Part1.VIN
  N4: Part1.VO-, SP1.-
  N5: Part1.VO+, SP1.+

custom parts:
  Adafruit MAX98357A I2S 3W Class D Amplifier: Listen to this good news - we now have an all in one digital audio amp breakout board that works incredibly well with the Raspberry Pi! If you're looking for an easy and low cost way to get you digital sound files bumpin' then the MAX08357 I2S Amp Breakout is for you. It takes standard I2S digital audio input and, not only decodes it into analog, but also amplifies it directly into a speaker.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
