# Fritzing sketch LCD Display (saved by Fritzing 0.9.3b)

parts:
  Raspberry_Pi_Zero1 = Raspberry Pi Zero
  Part1 = Seven-Segment LED Backpack 1.2 Inch Digits [part_number=1268]

nets:
  3V3: Raspberry_Pi_Zero1.3v3, Raspberry_Pi_Zero1.3V3, Part1.VCCIO
  N1: Raspberry_Pi_Zero1.GPIO2, Part1.SDA
  N2: Raspberry_Pi_Zero1.GPIO3, Part1.SCL
  GND: Raspberry_Pi_Zero1.GND, Part1.GND
  5V: Raspberry_Pi_Zero1.5V, Part1.VDD

custom parts:
  Seven-Segment LED Backpack 1.2 Inch Digits: This jumbo 1.2" 7-segment LED display includes a driver chip for simple control via an I2C interface. The backpack features address-selection jumpers so you can connect up to eight displays on a single I2C bus.
