# Fritzing sketch audio_amp (saved by Fritzing 0.9.2b)
breadboards: 1

parts:
  Part1 = Mono 2.5W Class D Audio Amplifier - PAM8302
  Raspberry_Pi_A1 = Raspberry Pi A
  SP1 = SPEAKER [package=pcb_mount_speaker]
  TRRS1 = Audio Jack (TRRS) 3.5mm [part_number="LUMBERG JEITA RC-5325A" package="RC-5325A [SMD]"]

nets:
  GND: Part1.GND, Raspberry_Pi_A1.GND
  VCC: Part1.VCC, Raspberry_Pi_A1.5V
  N1: Part1.AIN-, TRRS1.RING1
  N2: Part1.AIN+, TRRS1.RING2
  N3: Part1.VO+, SP1.+
  N4: Part1.VO-, SP1.-

custom parts:
  Mono 2.5W Class D Audio Amplifier - PAM8302: A super small but powerful mono amplifier able to deliver up to 2.5 Watts into 4-8 ohm impedance speakers. Inside the miniature chip is a class D controller, able to run from 2.0V-5.5VDC. Since the amp is a class D, its very efficient (over 90% efficient when driving an 8Ω speaker at over half a Watt) - making it perfect for portable and battery-powered projects.
